// Logisim project x86_processor.circ as structural Verilog: 11 circuits, main circuit main
module main (
  output [63:0] PC,
  output [63:0] valP,
  output [3:0] icode,
  output [3:0] code,
  output [63:0] valC,
  output [63:0] valM,
  output [63:0] valE,
  output [3:0] stat,
  output [3:0] rA,
  output [3:0] rB
);

  wire and_1_out, clock_1_out, d_ff_1_q, execute_1_cond, global_clock_1_decode, global_clock_1_execute,
       global_clock_1_fetch, global_clock_1_mem_read, global_clock_1_memory, global_clock_1_pc_update,
       global_clock_1_pc_wb, inst_and_need_1_halt, inst_and_need_1_irmovq, inst_and_need_1_needregid,
       inst_and_need_1_needvalc, inst_and_need_1_push_or_pop, inst_and_need_1_valid_inst,
       instruction_memory_1_imem_error, memory_1_dmem_error;
  wire [3:0] controlled_buffer_1_out, controlled_buffer_1_out_2, instruction_memory_1_byte0;
  wire [7:0] instruction_memory_1_byte1, instruction_memory_1_byte2, instruction_memory_1_byte3,
       instruction_memory_1_byte4, instruction_memory_1_byte5, instruction_memory_1_byte6,
       instruction_memory_1_byte7, instruction_memory_1_byte8, instruction_memory_1_byte9;
  wire [63:0] decode_1_vala, decode_1_valb, pc_update_1_newpc;

  Clock clock_1 (.out(clock_1_out));
  Global_Clock global_clock_1 (
    .in_1(and_1_out), .Fetch(global_clock_1_fetch), .Decode(global_clock_1_decode),
    .Execute(global_clock_1_execute), .Memory(global_clock_1_memory), .PC_WB(global_clock_1_pc_wb),
    .PC_update(global_clock_1_pc_update), .mem_read(global_clock_1_mem_read));
  and and_1 (and_1_out, clock_1_out, ~d_ff_1_q);  // AND_Gate
  D_Flip_Flop #(.trigger("falling")) d_ff_1 (
    .D(inst_and_need_1_halt), .clk(clock_1_out), .Q(d_ff_1_q));  // open: Qn, preset, reset
  PC_increment pc_increment_1 (
    .i(inst_and_need_1_needvalc), .r(inst_and_need_1_needregid), .PC(PC), .clk(global_clock_1_decode),
    .ValP(valP));
  instruction_memory instruction_memory_1 (
    .PC(pc_update_1_newpc), .clk(global_clock_1_fetch), .byte0({code, instruction_memory_1_byte0}),
    .byte1(instruction_memory_1_byte1), .byte2(instruction_memory_1_byte2),
    .byte3(instruction_memory_1_byte3), .byte4(instruction_memory_1_byte4),
    .byte5(instruction_memory_1_byte5), .byte6(instruction_memory_1_byte6),
    .byte7(instruction_memory_1_byte7), .byte8(instruction_memory_1_byte8),
    .byte9(instruction_memory_1_byte9), .imem_error(instruction_memory_1_imem_error), .outPC(PC));
  assign {controlled_buffer_1_out_2, controlled_buffer_1_out} = inst_and_need_1_needregid ? instruction_memory_1_byte1 : 8'bz;  // Controlled_Buffer controlled_buffer_1
  Multiplexer #(.width(8)) multiplexer_1 (
    .in0(instruction_memory_1_byte1), .in1(instruction_memory_1_byte2), .out(valC[7:0]),
    .sel(inst_and_need_1_needregid));
  Multiplexer #(.width(8)) multiplexer_2 (
    .in0(instruction_memory_1_byte2), .in1(instruction_memory_1_byte3), .out(valC[15:8]),
    .sel(inst_and_need_1_needregid));
  Multiplexer #(.width(8)) multiplexer_3 (
    .in0(instruction_memory_1_byte3), .in1(instruction_memory_1_byte4), .out(valC[23:16]),
    .sel(inst_and_need_1_needregid));
  Multiplexer #(.width(8)) multiplexer_4 (
    .in0(instruction_memory_1_byte4), .in1(instruction_memory_1_byte5), .out(valC[31:24]),
    .sel(inst_and_need_1_needregid));
  Multiplexer #(.width(8)) multiplexer_5 (
    .in0(instruction_memory_1_byte5), .in1(instruction_memory_1_byte6), .out(valC[39:32]),
    .sel(inst_and_need_1_needregid));
  Multiplexer #(.width(8)) multiplexer_6 (
    .in0(instruction_memory_1_byte6), .in1(instruction_memory_1_byte7), .out(valC[47:40]),
    .sel(inst_and_need_1_needregid));
  Multiplexer #(.width(8)) multiplexer_7 (
    .in0(instruction_memory_1_byte7), .in1(instruction_memory_1_byte8), .out(valC[55:48]),
    .sel(inst_and_need_1_needregid));
  Multiplexer #(.width(8)) multiplexer_8 (
    .in0(instruction_memory_1_byte8), .in1(instruction_memory_1_byte9), .out(valC[63:56]),
    .sel(inst_and_need_1_needregid));
  Inst_and_Need inst_and_need_1 (
    .in_1(code[0]), .in_2(code[1]), .in_3(code[2]), .in_4(code[3]), .halt(inst_and_need_1_halt),
    .irmovq(inst_and_need_1_irmovq), .needValC(inst_and_need_1_needvalc),
    .needRegID(inst_and_need_1_needregid), .push_or_pop(inst_and_need_1_push_or_pop),
    .valid_inst(inst_and_need_1_valid_inst));  // open: nop
  Multiplexer #(.width(4)) multiplexer_9 (
    .in0(controlled_buffer_1_out_2), .in1(4'b1111), .out(rA), .sel(inst_and_need_1_irmovq));
  Multiplexer #(.width(4)) multiplexer_10 (
    .in0(controlled_buffer_1_out), .in1(4'b1111), .out(rB), .sel(inst_and_need_1_push_or_pop));
  PC_Update pc_update_1 (
    .cond(execute_1_cond), .icode(code), .valC(valC), .valP(valP), .valM(valM),
    .clk(global_clock_1_pc_update), .newPC(pc_update_1_newpc));
  decode decode_1 (
    .M(valM), .E(valE), .cond(execute_1_cond), .icode(code), .rA(rA), .rB(rB), .clk(global_clock_1_decode),
    .clkwb(global_clock_1_pc_wb), .valA(decode_1_vala), .valB(decode_1_valb));
  execute execute_1 (
    .icode(code), .ifun(instruction_memory_1_byte0), .valC(valC), .valA(decode_1_vala), .valB(decode_1_valb),
    .clk(global_clock_1_execute), .valE(valE), .cond(execute_1_cond));
  memory memory_1 (
    .icode(code), .valE(valE), .valA(decode_1_vala), .valP(valP), .clk(global_clock_1_memory),
    .mem_read(global_clock_1_mem_read), .dmem_error(memory_1_dmem_error), .valM(valM));
  status status_1 (
    .icode(inst_and_need_1_halt), .imem_error(instruction_memory_1_imem_error),
    .instr_valid(inst_and_need_1_valid_inst), .dmem_error(memory_1_dmem_error), .stat(stat));

  assign icode = code;

  // Notes on the sheet:
  //   shift for valC: 1-8 or 2-9
  //   ifun
  //   icode
  //   irmovq
  //   valC
  //   rA
  //   rB
  //   write back stage for execute and memory
endmodule

module instruction_memory (
  input  [63:0] PC,
  input  clk,
  output [7:0] byte0,
  output [7:0] byte1,
  output [7:0] byte2,
  output [7:0] byte3,
  output [7:0] byte4,
  output [7:0] byte5,
  output [7:0] byte6,
  output [7:0] byte7,
  output [7:0] byte8,
  output [7:0] byte9,
  output imem_error,
  output [63:0] outPC
);

  wire comparator_1_eq, comparator_2_eq, comparator_3_eq, comparator_4_eq, comparator_5_eq, comparator_6_eq,
       comparator_7_eq, comparator_8_eq, comparator_9_eq, comparator_10_eq, comparator_11_eq;
  wire [3:0] counter_1_q;
  wire [7:0] demultiplexer_1_out0, demultiplexer_1_out1, demultiplexer_1_out2, demultiplexer_1_out3,
       demultiplexer_1_out4, demultiplexer_1_out5, demultiplexer_1_out6, demultiplexer_1_out7,
       demultiplexer_1_out8, demultiplexer_1_out9, rom_1_data;
  wire [11:0] adder_1_out, bit_extender_1_out;

  assign bit_extender_1_out = {{8{1'b0}}, counter_1_q};  // Bit_Extender bit_extender_1
  Adder #(.width(12)) adder_1 (.a(PC[11:0]), .b(bit_extender_1_out), .out(adder_1_out));  // open: cin, cout
  ROM #(.addrWidth(12)) rom_1 (.addr(adder_1_out), .data(rom_1_data));
  Counter #(.max('hf), .width(4)) counter_1 (
    .D(4'b1011), .Q(counter_1_q), .up(1'b1), .clk(clk), .clr(comparator_1_eq));  // open: load, count, carry
  Comparator #(.width(4)) comparator_1 (.a(4'b1011), .b(counter_1_q), .eq(comparator_1_eq));  // open: gt, lt
  Demultiplexer #(.select(4), .width(8)) demultiplexer_1 (
    .out0(demultiplexer_1_out0), .out1(demultiplexer_1_out1), .out2(demultiplexer_1_out2),
    .out3(demultiplexer_1_out3), .out4(demultiplexer_1_out4), .out5(demultiplexer_1_out5),
    .out6(demultiplexer_1_out6), .out7(demultiplexer_1_out7), .out8(demultiplexer_1_out8),
    .out9(demultiplexer_1_out9), .in(rom_1_data), .sel(counter_1_q));  // open: out10, out11, out12, out13, out14, out15
  Comparator #(.mode("unsigned"), .width(4)) comparator_2 (
    .a(4'b0000), .b(counter_1_q), .eq(comparator_2_eq));  // open: gt, lt
  Comparator #(.mode("unsigned"), .width(4)) comparator_3 (
    .a(counter_1_q), .b(4'b0001), .eq(comparator_3_eq));  // open: gt, lt
  Comparator #(.mode("unsigned"), .width(4)) comparator_4 (
    .a(counter_1_q), .b(4'b0010), .eq(comparator_4_eq));  // open: gt, lt
  Comparator #(.mode("unsigned"), .width(4)) comparator_5 (
    .a(counter_1_q), .b(4'b0011), .eq(comparator_5_eq));  // open: gt, lt
  Comparator #(.mode("unsigned"), .width(4)) comparator_6 (
    .a(counter_1_q), .b(4'b0100), .eq(comparator_6_eq));  // open: gt, lt
  Comparator #(.mode("unsigned"), .width(4)) comparator_7 (
    .a(counter_1_q), .b(4'b0101), .eq(comparator_7_eq));  // open: gt, lt
  Comparator #(.mode("unsigned"), .width(4)) comparator_8 (
    .a(counter_1_q), .b(4'b0110), .eq(comparator_8_eq));  // open: gt, lt
  Comparator #(.mode("unsigned"), .width(4)) comparator_9 (
    .a(counter_1_q), .b(4'b0111), .eq(comparator_9_eq));  // open: gt, lt
  Comparator #(.mode("unsigned"), .width(4)) comparator_10 (
    .a(counter_1_q), .b(4'b1000), .eq(comparator_10_eq));  // open: gt, lt
  Comparator #(.mode("unsigned"), .width(4)) comparator_11 (
    .a(counter_1_q), .b(4'b1001), .eq(comparator_11_eq));  // open: gt, lt
  Comparator #(.mode("unsigned"), .width(12)) comparator_12 (
    .a(PC[11:0]), .b(12'hff8), .gt(imem_error));  // open: eq, lt
  Register register_1 (.D(demultiplexer_1_out0), .en(comparator_2_eq), .clk(clk), .Q(byte0));  // open: clr
  Register register_2 (.D(demultiplexer_1_out1), .en(comparator_3_eq), .clk(clk), .Q(byte1));  // open: clr
  Register register_3 (.D(demultiplexer_1_out2), .en(comparator_4_eq), .clk(clk), .Q(byte2));  // open: clr
  Register register_4 (.D(demultiplexer_1_out3), .en(comparator_5_eq), .clk(clk), .Q(byte3));  // open: clr
  Register register_5 (.D(demultiplexer_1_out4), .en(comparator_6_eq), .clk(clk), .Q(byte4));  // open: clr
  Register register_6 (.D(demultiplexer_1_out5), .en(comparator_7_eq), .clk(clk), .Q(byte5));  // open: clr
  Register register_7 (.D(demultiplexer_1_out6), .en(comparator_8_eq), .clk(clk), .Q(byte6));  // open: clr
  Register register_8 (.D(demultiplexer_1_out7), .en(comparator_9_eq), .clk(clk), .Q(byte7));  // open: clr
  Register register_9 (.D(demultiplexer_1_out8), .en(comparator_10_eq), .clk(clk), .Q(byte8));  // open: clr
  Register register_10 (.D(demultiplexer_1_out9), .en(comparator_11_eq), .clk(clk), .Q(byte9));  // open: clr

  assign outPC = PC;

  // Notes on the sheet:
  //   contents of rom_1 (hex, n*v repeats v):
  //   30 f4 90 1 6*0 30 f0 2 7*0 30 f3 10 7*0 30 f8 1 7*0 40 84 8*0 30 f8 2 7*0 40 84 8 7*0 30 f8 3 7*0 40
  //   84 10 7*0 30 f8 4 7*0 40 84 18 7*0 30 f8 6 7*0 40 84 20 7*0 30 f8 9 7*0 40 84 28 7*0 30 f8 c 7*0 40
  //   84 30 7*0 30 f8 f 7*0 40 84 38 7*0 30 f2 8*0 60 42 30 f1 20 7*0 60 41 30 f5 8*0 60 15 30 fa 8 7*0 30
  //   fb 1 7*0 30 fc 2 7*0 30 fd 2 7*0 50 62 8*0 60 a2 50 81 8*0 60 a1 60 68 40 85 8*0 60 a5 61 bd 74 a 1
  //   6*0 61 bc 74 0 1
endmodule

module PC_increment (
  input  i,
  input  r,
  input  [63:0] PC,
  input  clk,
  output [63:0] ValP
);

  wire [3:0] bit_extender_1_out, multiplier_1_out;
  wire [63:0] adder_1_out, adder_2_out, bit_extender_2_out;

  assign bit_extender_1_out = {{3{1'b0}}, i};  // Bit_Extender bit_extender_1
  Multiplier #(.width(4)) multiplier_1 (
    .a(bit_extender_1_out), .b(4'b1000), .out(multiplier_1_out));  // open: cin, cout
  Adder #(.width(64)) adder_1 (.a(bit_extender_2_out), .b(PC), .out(adder_1_out), .cin(r));  // open: cout
  assign bit_extender_2_out = {{60{1'b0}}, multiplier_1_out};  // Bit_Extender bit_extender_2
  Adder #(.width(64)) adder_2 (.a(adder_1_out), .b(64'h1), .out(adder_2_out));  // open: cin, cout
  Register #(.width(64)) register_1 (.D(adder_2_out), .en(clk), .clk(clk), .Q(ValP));  // open: clr

  // Notes on the sheet:
  //   PC + r + 8*i
  //   8*i
  //   +1
endmodule

module decode (
  input  [63:0] M,
  input  [63:0] E,
  input  cond,
  input  [3:0] icode,
  input  [3:0] rA,
  input  [3:0] rB,
  input  clk,
  input  clkwb,
  output [63:0] valA,
  output [63:0] valB
);

  wire and_1_out, clock_1_out, comparator_1_eq, decoder_1_out2, decoder_1_out3, decoder_1_out6,
       decoder_1_out8, decoder_1_out9, decoder_1_out10, decoder_1_out11, decoder_2_out0, decoder_2_out1,
       decoder_2_out2, decoder_2_out3, decoder_2_out4, decoder_2_out5, decoder_2_out6, decoder_2_out7,
       decoder_2_out8, decoder_2_out9, decoder_2_out10, decoder_2_out11, decoder_2_out12, decoder_2_out13,
       decoder_2_out14, decoder_3_out5, decoder_3_out11, decoder_4_out0, decoder_4_out1, decoder_4_out2,
       decoder_4_out3, decoder_4_out4, decoder_4_out5, decoder_4_out6, decoder_4_out7, decoder_4_out8,
       decoder_4_out9, decoder_4_out10, decoder_4_out11, decoder_4_out12, decoder_4_out13, decoder_4_out14,
       decoder_5_out2, decoder_5_out4, decoder_5_out6, decoder_5_out9, decoder_5_out10, decoder_5_out11,
       decoder_6_out4, decoder_6_out5, decoder_6_out6, decoder_6_out8, decoder_6_out9, decoder_6_out10,
       decoder_6_out11, or_1_out, or_2_out, or_3_out, or_4_out, or_5_out, or_6_out, or_7_out, or_8_out,
       or_9_out, or_10_out, or_11_out, or_12_out, or_13_out, or_14_out, or_15_out, or_16_out, or_17_out,
       or_18_out, or_19_out, or_20_out, or_21_out, or_22_out, or_23_out;
  wire [3:0] multiplexer_8_out, multiplexer_10_out, multiplexer_12_out, multiplexer_15_out,
       multiplexer_16_out, multiplexer_18_out, multiplexer_19_out;
  wire [7:0] counter_1_q;
  wire [63:0] multiplexer_1_out, multiplexer_2_out, multiplexer_4_out, multiplexer_5_out, multiplexer_6_out,
       multiplexer_7_out, multiplexer_9_out, multiplexer_11_out, multiplexer_13_out, multiplexer_14_out,
       multiplexer_17_out, multiplexer_20_out, multiplexer_21_out, multiplexer_22_out, multiplexer_23_out,
       r8_q, r9_q, r10_q, r11_q, r12_q, r13_q, r14_q, rax_q, rbp_q, rbx_q, rcx_q, rdi_q, rdx_q, rsi_q, rsp_q;

  or or_1 (or_1_out, clkwb, clk);
  Multiplexer #(.width(64)) multiplexer_1 (.in0(E), .in1(M), .out(multiplexer_1_out), .sel(decoder_4_out0));
  Register #(.width(64)) rax (.D(multiplexer_1_out), .en(or_2_out), .clk(or_1_out), .Q(rax_q));  // open: clr
  or or_2 (or_2_out, decoder_2_out0, decoder_4_out0);
  Multiplexer #(.width(64)) multiplexer_2 (.in0(E), .in1(M), .out(multiplexer_2_out), .sel(decoder_4_out1));
  Multiplexer #(.select(4), .width(64)) multiplexer_3 (
    .in0(rax_q), .in1(rcx_q), .in2(rdx_q), .in3(rbx_q), .in4(rsp_q), .in5(rbp_q), .in6(rsi_q), .in7(rdi_q),
    .in8(r8_q), .in9(r9_q), .in10(r10_q), .in11(r11_q), .in12(r12_q), .in13(r13_q), .in14(r14_q), .out(valA),
    .sel(multiplexer_16_out));  // open: in15
  Register #(.width(64)) rcx (.D(multiplexer_2_out), .en(or_3_out), .clk(or_1_out), .Q(rcx_q));  // open: clr
  or or_3 (or_3_out, decoder_2_out1, decoder_4_out1);
  Multiplexer #(.width(64)) multiplexer_4 (.in0(E), .in1(M), .out(multiplexer_4_out), .sel(decoder_4_out2));
  Register #(.width(64)) rdx (.D(multiplexer_4_out), .en(or_4_out), .clk(or_1_out), .Q(rdx_q));  // open: clr
  or or_4 (or_4_out, decoder_2_out2, decoder_4_out2);
  Multiplexer #(.width(64)) multiplexer_5 (.in0(E), .in1(M), .out(multiplexer_5_out), .sel(decoder_4_out3));
  Register #(.width(64)) rbx (.D(multiplexer_5_out), .en(or_5_out), .clk(or_1_out), .Q(rbx_q));  // open: clr
  or or_5 (or_5_out, decoder_2_out3, decoder_4_out3);
  Multiplexer #(.width(64)) multiplexer_6 (.in0(E), .in1(M), .out(multiplexer_6_out), .sel(decoder_4_out4));
  Register #(.width(64)) rsp (.D(multiplexer_6_out), .en(or_6_out), .clk(or_1_out), .Q(rsp_q));  // open: clr
  or or_6 (or_6_out, decoder_2_out4, decoder_4_out4);
  Counter #(.max('h15)) counter_1 (.Q(counter_1_q), .clk(clock_1_out));  // open: load, D, count, carry, up, clr
  Clock clock_1 (.out(clock_1_out));
  Comparator comparator_1 (.a(counter_1_q), .b(8'h15), .eq(comparator_1_eq));  // open: gt, lt
  and and_1 (and_1_out, cond, decoder_1_out2);
  Decoder #(.select(4)) decoder_1 (
    .out2(decoder_1_out2), .out3(decoder_1_out3), .out6(decoder_1_out6), .out8(decoder_1_out8),
    .out9(decoder_1_out9), .out10(decoder_1_out10), .out11(decoder_1_out11), .sel(icode));  // open: out0, out1, out4, out5, out7, out12, out13, out14, out15, en
  Register #(.width(64)) rbp (.D(multiplexer_7_out), .en(or_7_out), .clk(or_1_out), .Q(rbp_q));  // open: clr
  or or_7 (or_7_out, decoder_2_out5, decoder_4_out5);
  Multiplexer #(.width(64)) multiplexer_7 (.in0(E), .in1(M), .out(multiplexer_7_out), .sel(decoder_4_out5));
  or or_8 (or_8_out, decoder_1_out8, decoder_1_out9, decoder_1_out10, decoder_1_out11);
  Multiplexer #(.width(4)) multiplexer_8 (.in0(4'b1111), .in1(rB), .out(multiplexer_8_out), .sel(or_9_out));
  or or_9 (or_9_out, and_1_out, decoder_1_out3, decoder_1_out6);
  or or_10 (or_10_out, decoder_2_out6, decoder_4_out6);
  Multiplexer #(.width(64)) multiplexer_9 (.in0(E), .in1(M), .out(multiplexer_9_out), .sel(decoder_4_out6));
  Decoder #(.select(4)) decoder_2 (
    .out0(decoder_2_out0), .out1(decoder_2_out1), .out2(decoder_2_out2), .out3(decoder_2_out3),
    .out4(decoder_2_out4), .out5(decoder_2_out5), .out6(decoder_2_out6), .out7(decoder_2_out7),
    .out8(decoder_2_out8), .out9(decoder_2_out9), .out10(decoder_2_out10), .out11(decoder_2_out11),
    .out12(decoder_2_out12), .out13(decoder_2_out13), .out14(decoder_2_out14), .sel(multiplexer_10_out),
    .en(comparator_1_eq));  // open: out15
  Multiplexer #(.width(4)) multiplexer_10 (
    .in0(multiplexer_8_out), .in1(4'b0100), .out(multiplexer_10_out), .sel(or_8_out));
  Decoder #(.select(4)) decoder_3 (
    .out5(decoder_3_out5), .out11(decoder_3_out11), .sel(icode));  // open: out0, out1, out2, out3, out4, out6, out7, out8, out9, out10, out12, out13, out14, out15, en
  Register #(.width(64)) rsi (.D(multiplexer_9_out), .en(or_10_out), .clk(or_1_out), .Q(rsi_q));  // open: clr
  Multiplexer #(.width(64)) multiplexer_11 (.in0(E), .in1(M), .out(multiplexer_11_out), .sel(decoder_4_out7));
  or or_11 (or_11_out, decoder_3_out5, decoder_3_out11);
  Register #(.width(64)) rdi (.D(multiplexer_11_out), .en(or_12_out), .clk(or_1_out), .Q(rdi_q));  // open: clr
  or or_12 (or_12_out, decoder_2_out7, decoder_4_out7);
  Decoder #(.select(4)) decoder_4 (
    .out0(decoder_4_out0), .out1(decoder_4_out1), .out2(decoder_4_out2), .out3(decoder_4_out3),
    .out4(decoder_4_out4), .out5(decoder_4_out5), .out6(decoder_4_out6), .out7(decoder_4_out7),
    .out8(decoder_4_out8), .out9(decoder_4_out9), .out10(decoder_4_out10), .out11(decoder_4_out11),
    .out12(decoder_4_out12), .out13(decoder_4_out13), .out14(decoder_4_out14), .sel(multiplexer_12_out),
    .en(comparator_1_eq));  // open: out15
  Multiplexer #(.width(4)) multiplexer_12 (.in0(4'b1111), .in1(rA), .out(multiplexer_12_out), .sel(or_11_out));
  Multiplexer #(.width(64)) multiplexer_13 (.in0(E), .in1(M), .out(multiplexer_13_out), .sel(decoder_4_out8));
  Decoder #(.select(4)) decoder_5 (
    .out2(decoder_5_out2), .out4(decoder_5_out4), .out6(decoder_5_out6), .out9(decoder_5_out9),
    .out10(decoder_5_out10), .out11(decoder_5_out11), .sel(icode));  // open: out0, out1, out3, out5, out7, out8, out12, out13, out14, out15, en
  Register #(.width(64)) r8 (.D(multiplexer_13_out), .en(or_13_out), .clk(or_1_out), .Q(r8_q));  // open: clr
  or or_13 (or_13_out, decoder_2_out8, decoder_4_out8);
  Multiplexer #(.width(64)) multiplexer_14 (.in0(E), .in1(M), .out(multiplexer_14_out), .sel(decoder_4_out9));
  or or_14 (or_14_out, decoder_5_out9, decoder_5_out11);
  Multiplexer #(.width(4)) multiplexer_15 (.in0(4'b1111), .in1(rA), .out(multiplexer_15_out), .sel(or_15_out));
  or or_15 (or_15_out, decoder_5_out2, decoder_5_out4, decoder_5_out6, decoder_5_out10);
  Register #(.width(64)) r9 (.D(multiplexer_14_out), .en(or_16_out), .clk(or_1_out), .Q(r9_q));  // open: clr
  or or_16 (or_16_out, decoder_2_out9, decoder_4_out9);
  Multiplexer #(.width(4)) multiplexer_16 (
    .in0(multiplexer_15_out), .in1(4'b0100), .out(multiplexer_16_out), .sel(or_14_out));
  Decoder #(.select(4)) decoder_6 (
    .out4(decoder_6_out4), .out5(decoder_6_out5), .out6(decoder_6_out6), .out8(decoder_6_out8),
    .out9(decoder_6_out9), .out10(decoder_6_out10), .out11(decoder_6_out11), .sel(icode));  // open: out0, out1, out2, out3, out7, out12, out13, out14, out15, en
  Multiplexer #(.width(64)) multiplexer_17 (.in0(E), .in1(M), .out(multiplexer_17_out), .sel(decoder_4_out10));
  Register #(.width(64)) r10 (.D(multiplexer_17_out), .en(or_17_out), .clk(or_1_out), .Q(r10_q));  // open: clr
  or or_17 (or_17_out, decoder_2_out10, decoder_4_out10);
  or or_18 (or_18_out, decoder_6_out8, decoder_6_out9, decoder_6_out10, decoder_6_out11);
  or or_19 (or_19_out, decoder_6_out4, decoder_6_out5, decoder_6_out6);
  Multiplexer #(.width(4)) multiplexer_18 (
    .in0(multiplexer_19_out), .in1(4'b0100), .out(multiplexer_18_out), .sel(or_18_out));
  Multiplexer #(.width(4)) multiplexer_19 (.in0(4'b1111), .in1(rB), .out(multiplexer_19_out), .sel(or_19_out));
  Register #(.width(64)) r11 (.D(multiplexer_20_out), .en(or_20_out), .clk(or_1_out), .Q(r11_q));  // open: clr
  or or_20 (or_20_out, decoder_2_out11, decoder_4_out11);
  Multiplexer #(.width(64)) multiplexer_20 (.in0(E), .in1(M), .out(multiplexer_20_out), .sel(decoder_4_out11));
  or or_21 (or_21_out, decoder_2_out12, decoder_4_out12);
  Multiplexer #(.width(64)) multiplexer_21 (.in0(E), .in1(M), .out(multiplexer_21_out), .sel(decoder_4_out12));
  Register #(.width(64)) r12 (.D(multiplexer_21_out), .en(or_21_out), .clk(or_1_out), .Q(r12_q));  // open: clr
  or or_22 (or_22_out, decoder_2_out13, decoder_4_out13);
  Multiplexer #(.width(64)) multiplexer_22 (.in0(E), .in1(M), .out(multiplexer_22_out), .sel(decoder_4_out13));
  Register #(.width(64)) r13 (.D(multiplexer_22_out), .en(or_22_out), .clk(or_1_out), .Q(r13_q));  // open: clr
  Multiplexer #(.width(64)) multiplexer_23 (.in0(E), .in1(M), .out(multiplexer_23_out), .sel(decoder_4_out14));
  Register #(.width(64)) r14 (.D(multiplexer_23_out), .en(or_23_out), .clk(or_1_out), .Q(r14_q));  // open: clr
  or or_23 (or_23_out, decoder_2_out14, decoder_4_out14);
  Multiplexer #(.select(4), .width(64)) multiplexer_24 (
    .in0(rax_q), .in1(rcx_q), .in2(rdx_q), .in3(rbx_q), .in4(rsp_q), .in5(rbp_q), .in6(rsi_q), .in7(rdi_q),
    .in8(r8_q), .in9(r9_q), .in10(r10_q), .in11(r11_q), .in12(r12_q), .in13(r13_q), .in14(r14_q), .out(valB),
    .sel(multiplexer_18_out));  // open: in15

  // Notes on the sheet:
  //   read1
  //   dstE
  //   dstM
  //   write1
  //   write2
  //   srcA
  //   srcB
  //   read2
endmodule

module execute (
  input  [3:0] icode,
  input  [3:0] ifun,
  input  [63:0] valC,
  input  [63:0] valA,
  input  [63:0] valB,
  input  clk,
  output [63:0] valE,
  output cond
);

  wire and_1_out, and_2_out, and_3_out, and_5_out, and_6_out, bitselector_1_out, bitselector_2_out,
       bitselector_3_out, comparator_1_eq, not_1_out, not_2_out, not_3_out, not_4_out, not_5_out, not_7_out,
       or_1_out, register_1_q, register_2_q, register_3_q, xnor_1_out, xor_1_out, xor_2_out;
  wire [1:0] bit_extender_2_out, multiplexer_4_out;
  wire [2:0] bit_extender_1_out;
  wire [63:0] and_4_out, multiplexer_2_out, multiplexer_3_out, multiplexer_5_out, multiplexer_6_out,
       not_6_out, xor_3_out;

  or or_1 (or_1_out, register_1_q, xor_1_out);
  Multiplexer #(.enable("true"), .select(3)) multiplexer_1 (
    .in0(1'b1), .in1(or_1_out), .in2(xor_1_out), .in3(register_1_q), .in4(not_1_out), .in5(not_2_out),
    .in6(and_1_out), .out(cond), .sel(bit_extender_1_out));  // open: in7, en
  not not_1 (not_1_out, register_1_q);
  not not_2 (not_2_out, xor_1_out);
  not not_3 (not_3_out, register_1_q);
  xor xor_1 (xor_1_out, register_3_q, register_2_q);
  and and_1 (and_1_out, not_3_out, not_2_out);
  Bit_Extender #(.in_width(4), .out_width(3), .\type ("zero")) bit_extender_1 (.in(ifun), .out(bit_extender_1_out));
  and and_2 (and_2_out, not_4_out, icode[2], icode[1], not_5_out);
  not not_4 (not_4_out, icode[3]);
  Register #(.width(1)) register_1 (.D(comparator_1_eq), .en(and_2_out), .clk(clk), .Q(register_1_q));  // open: clr
  Register #(.width(1)) register_2 (.D(bitselector_1_out), .en(and_2_out), .clk(clk), .Q(register_2_q));  // open: clr
  Register #(.width(1)) register_3 (.D(and_3_out), .en(and_2_out), .clk(clk), .Q(register_3_q));  // open: clr
  not not_5 (not_5_out, icode[0]);
  and and_3 (and_3_out, xor_2_out, xnor_1_out);
  Multiplexer #(.select(2), .width(64)) multiplexer_2 (
    .in0(multiplexer_3_out), .in1(not_6_out), .in2(and_4_out), .in3(xor_3_out), .out(multiplexer_2_out),
    .sel(multiplexer_4_out));
  assign not_6_out = ~multiplexer_3_out;  // NOT_Gate not_6, 64 bits wide
  Multiplexer #(.select(4), .width(64)) multiplexer_3 (
    .in2(valA), .in3(valC), .in4(valC), .in5(valC), .in6(valA), .in8(64'hfffffffffffffff8), .in9(64'h8),
    .in10(64'hfffffffffffffff8), .in11(64'h8), .out(multiplexer_3_out), .sel(icode));  // open: in0, in1, in7, in12, in13, in14, in15
  xor xor_2 (xor_2_out, bitselector_1_out, bitselector_2_out);
  xnor xnor_1 (xnor_1_out, bitselector_2_out, bitselector_3_out);
  assign and_4_out = multiplexer_3_out & multiplexer_6_out;  // AND_Gate and_4, 64 bits wide
  assign xor_3_out = multiplexer_3_out ^ multiplexer_6_out;  // XOR_Gate xor_3, 64 bits wide
  BitSelector #(.width(64)) bitselector_1 (.in(valE), .out(bitselector_1_out), .sel({6{1'b1}}));
  BitSelector #(.width(64)) bitselector_2 (.in(multiplexer_2_out), .out(bitselector_2_out), .sel({6{1'b1}}));
  BitSelector #(.width(64)) bitselector_3 (.in(multiplexer_5_out), .out(bitselector_3_out), .sel({6{1'b1}}));
  Multiplexer #(.width(2)) multiplexer_4 (
    .in0(2'b00), .in1(bit_extender_2_out), .out(multiplexer_4_out), .sel(and_5_out));
  Comparator #(.width(64)) comparator_1 (.a({64{1'b0}}), .b(valE), .eq(comparator_1_eq));  // open: gt, lt
  Multiplexer #(.select(2), .width(64)) multiplexer_5 (
    .in0(multiplexer_6_out), .in1(multiplexer_6_out), .in2({64{1'b0}}), .in3({64{1'b0}}),
    .out(multiplexer_5_out), .sel(multiplexer_4_out));
  and and_5 (and_5_out, icode[1], icode[2]);
  Multiplexer #(.select(4), .width(64)) multiplexer_6 (
    .in2({64{1'b0}}), .in3({64{1'b0}}), .in4(valB), .in5(valB), .in6(valB), .in8(valB), .in9(valB),
    .in10(valB), .in11(valB), .out(multiplexer_6_out), .sel(icode));  // open: in0, in1, in7, in12, in13, in14, in15
  Adder #(.width(64)) adder_1 (
    .a(multiplexer_5_out), .b(multiplexer_2_out), .out(valE), .cin(and_6_out));  // open: cout
  and and_6 (and_6_out, multiplexer_4_out[0], not_7_out);
  not not_7 (not_7_out, multiplexer_4_out[1]);
  Bit_Extender #(.in_width(4), .out_width(2), .\type ("zero")) bit_extender_2 (.in(ifun), .out(bit_extender_2_out));

  // Notes on the sheet:
  //   le
  //   l
  //   e
  //   ne
  //   ge
  //   g
endmodule

module PC_Update (
  input  cond,
  input  [3:0] icode,
  input  [63:0] valC,
  input  [63:0] valP,
  input  [63:0] valM,
  input  clk,
  output [63:0] newPC
);

  wire and_1_out, comparator_1_eq;
  wire [63:0] multiplexer_1_out, multiplexer_2_out;

  and and_1 (and_1_out, cond, comparator_1_eq);
  Multiplexer #(.width(64)) multiplexer_1 (.in0(valP), .in1(valC), .out(multiplexer_1_out), .sel(and_1_out));
  Comparator #(.mode("unsigned"), .width(4)) comparator_1 (
    .a(icode), .b(4'b0111), .eq(comparator_1_eq));  // open: gt, lt
  Multiplexer #(.select(4), .width(64)) multiplexer_2 (
    .in1(valP), .in2(valP), .in3(valP), .in4(valP), .in5(valP), .in6(valP), .in7(multiplexer_1_out),
    .in10(valP), .in11(valP), .out(multiplexer_2_out), .sel(icode));  // open: in0, in8, in9, in12, in13, in14, in15
  Register #(.width(64)) register_1 (.D(multiplexer_2_out), .en(clk), .clk(clk), .Q(newPC));  // open: clr

  // Notes on the sheet:
  //   jump (7) instruction: chose valp or valc
  //   valM used during return/call operations
endmodule

module data_memory (
  input  [11:0] address,
  input  write_en,
  input  read_en,
  input  [63:0] data_in,
  input  clk,
  input  mem_read,
  output dmem_error,
  output [7:0] byte0,
  output [7:0] byte1,
  output [7:0] byte2,
  output [7:0] byte3,
  output [7:0] byte4,
  output [7:0] byte5,
  output [7:0] byte6,
  output [7:0] byte7
);

  wire decoder_1_out0, decoder_1_out1, decoder_1_out2, decoder_1_out3, decoder_1_out4, decoder_1_out5,
       decoder_1_out6, decoder_1_out7, or_1_out;
  wire [2:0] bit_extender_1_out;
  wire [7:0] demultiplexer_1_out0, demultiplexer_1_out1, demultiplexer_1_out2, demultiplexer_1_out3,
       demultiplexer_1_out4, demultiplexer_1_out5, demultiplexer_1_out6, demultiplexer_1_out7,
       multiplexer_1_out, ram_1_dout;
  wire [11:0] adder_1_out, counter_1_q;

  Multiplexer #(.select(3), .width(8)) multiplexer_1 (
    .in0(data_in[7:0]), .in1(data_in[15:8]), .in2(data_in[23:16]), .in3(data_in[31:24]),
    .in4(data_in[39:32]), .in5(data_in[47:40]), .in6(data_in[55:48]), .in7(data_in[63:56]),
    .out(multiplexer_1_out), .sel(bit_extender_1_out));
  Counter #(.max('h7), .width(12)) counter_1 (.Q(counter_1_q), .clk(clk));  // open: load, D, count, carry, up, clr
  Comparator #(.mode("unsigned"), .width(12)) comparator_1 (.a(address), .b(12'hff8), .gt(dmem_error));  // open: eq, lt
  RAM #(.addrWidth(12)) ram_1 (
    .addr(adder_1_out), .we(write_en), .oe(read_en), .clk(clk), .din(multiplexer_1_out), .dout(ram_1_dout));
  Adder #(.width(12)) adder_1 (.a(address), .b(counter_1_q), .out(adder_1_out));  // open: cin, cout
  Bit_Extender #(.in_width(12), .out_width(3)) bit_extender_1 (.in(counter_1_q), .out(bit_extender_1_out));
  or or_1 (or_1_out, clk, mem_read);
  Demultiplexer #(.select(3), .width(8)) demultiplexer_1 (
    .out0(demultiplexer_1_out0), .out1(demultiplexer_1_out1), .out2(demultiplexer_1_out2),
    .out3(demultiplexer_1_out3), .out4(demultiplexer_1_out4), .out5(demultiplexer_1_out5),
    .out6(demultiplexer_1_out6), .out7(demultiplexer_1_out7), .in(ram_1_dout), .sel(bit_extender_1_out));
  Decoder #(.select(3)) decoder_1 (
    .out0(decoder_1_out0), .out1(decoder_1_out1), .out2(decoder_1_out2), .out3(decoder_1_out3),
    .out4(decoder_1_out4), .out5(decoder_1_out5), .out6(decoder_1_out6), .out7(decoder_1_out7),
    .sel(bit_extender_1_out), .en(read_en));
  Register register_1 (.D(demultiplexer_1_out1), .en(decoder_1_out1), .clk(or_1_out), .Q(byte0));  // open: clr
  Register register_2 (.D(demultiplexer_1_out2), .en(decoder_1_out2), .clk(or_1_out), .Q(byte1));  // open: clr
  Register register_3 (.D(demultiplexer_1_out3), .en(decoder_1_out3), .clk(or_1_out), .Q(byte2));  // open: clr
  Register register_4 (.D(demultiplexer_1_out4), .en(decoder_1_out4), .clk(or_1_out), .Q(byte3));  // open: clr
  Register register_5 (.D(demultiplexer_1_out5), .en(decoder_1_out5), .clk(or_1_out), .Q(byte4));  // open: clr
  Register register_6 (.D(demultiplexer_1_out6), .en(decoder_1_out6), .clk(or_1_out), .Q(byte5));  // open: clr
  Register register_7 (.D(demultiplexer_1_out7), .en(decoder_1_out7), .clk(or_1_out), .Q(byte6));  // open: clr
  Register register_8 (.D(demultiplexer_1_out0), .en(decoder_1_out0), .clk(or_1_out), .Q(byte7));  // open: clr
endmodule

module memory (
  input  [3:0] icode,
  input  [63:0] valE,
  input  [63:0] valA,
  input  [63:0] valP,
  input  clk,
  input  mem_read,
  output dmem_error,
  output [63:0] valM
);

  wire decoder_1_out4, decoder_1_out5, decoder_1_out8, decoder_1_out9, decoder_1_out10, decoder_1_out11,
       or_1_out, read_out, write_out;
  wire [11:0] bit_extender_1_out, bit_extender_2_out, multiplexer_1_out;
  wire [63:0] multiplexer_2_out;

  Decoder #(.select(4)) decoder_1 (
    .out4(decoder_1_out4), .out5(decoder_1_out5), .out8(decoder_1_out8), .out9(decoder_1_out9),
    .out10(decoder_1_out10), .out11(decoder_1_out11), .sel(icode));  // open: out0, out1, out2, out3, out6, out7, out12, out13, out14, out15, en
  or read (read_out, decoder_1_out5, decoder_1_out9, decoder_1_out11);
  or write (write_out, decoder_1_out4, decoder_1_out8, decoder_1_out10);
  Multiplexer #(.width(12)) multiplexer_1 (
    .in0(bit_extender_1_out), .in1(bit_extender_2_out), .out(multiplexer_1_out), .sel(or_1_out));
  or or_1 (or_1_out, decoder_1_out9, decoder_1_out11);
  Bit_Extender #(.in_width(64), .out_width(12)) bit_extender_1 (.in(valE), .out(bit_extender_1_out));
  Bit_Extender #(.in_width(64), .out_width(12)) bit_extender_2 (.in(valA), .out(bit_extender_2_out));
  Multiplexer #(.width(64)) multiplexer_2 (.in0(valA), .in1(valP), .out(multiplexer_2_out), .sel(decoder_1_out8));
  data_memory data_memory_1 (
    .address(multiplexer_1_out), .write_en(write_out), .read_en(read_out), .data_in(multiplexer_2_out),
    .clk(clk), .mem_read(mem_read), .dmem_error(dmem_error), .byte0(valM[7:0]), .byte1(valM[15:8]),
    .byte2(valM[23:16]), .byte3(valM[31:24]), .byte4(valM[39:32]), .byte5(valM[47:40]), .byte6(valM[55:48]),
    .byte7(valM[63:56]));
endmodule

module status (
  input  icode,
  input  imem_error,
  input  instr_valid,
  input  dmem_error,
  output [3:0] stat
);

  not not_1 (stat[1], instr_valid);

  assign {stat[3:2], stat[0]} = {icode, imem_error, dmem_error};

  // Notes on the sheet:
  //   halt: icode=1
endmodule

module Global_Clock (
  input  in_1,
  output Fetch,
  output Decode,
  output Execute,
  output Memory,
  output PC_WB,
  output PC_update,
  output mem_read
);

  wire comparator_1_eq, decoder_1_out0, decoder_1_out1, decoder_1_out2, decoder_1_out3, decoder_1_out4,
       decoder_1_out5, decoder_1_out6, decoder_1_out7, decoder_1_out8, decoder_1_out9, decoder_1_out10,
       decoder_1_out11, decoder_1_out12, decoder_1_out13, decoder_1_out14, decoder_1_out15, decoder_1_out16,
       decoder_1_out17, decoder_1_out18, decoder_1_out19, decoder_1_out20, decoder_1_out21, FIRST10_out,
       MEM8_out, or_1_out;
  wire [4:0] counter_1_q;

  Counter #(.max('h1f), .width(5)) counter_1 (
    .Q(counter_1_q), .up(1'b1), .clk(in_1), .clr(comparator_1_eq));  // open: load, D, count, carry
  Comparator #(.mode("unsigned"), .width(5)) comparator_1 (
    .a(counter_1_q), .b(5'b10110), .eq(comparator_1_eq));  // open: gt, lt
  Decoder #(.select(5)) decoder_1 (
    .out0(decoder_1_out0), .out1(decoder_1_out1), .out2(decoder_1_out2), .out3(decoder_1_out3),
    .out4(decoder_1_out4), .out5(decoder_1_out5), .out6(decoder_1_out6), .out7(decoder_1_out7),
    .out8(decoder_1_out8), .out9(decoder_1_out9), .out10(decoder_1_out10), .out11(decoder_1_out11),
    .out12(decoder_1_out12), .out13(decoder_1_out13), .out14(decoder_1_out14), .out15(decoder_1_out15),
    .out16(decoder_1_out16), .out17(decoder_1_out17), .out18(decoder_1_out18), .out19(decoder_1_out19),
    .out20(decoder_1_out20), .out21(decoder_1_out21), .sel(counter_1_q));  // open: out22, out23, out24, out25, out26, out27, out28, out29, out30, out31, en
  or or_1 (or_1_out, decoder_1_out20, decoder_1_out19);
  or FIRST10 (FIRST10_out, decoder_1_out0, decoder_1_out1, decoder_1_out2, decoder_1_out3, decoder_1_out4, decoder_1_out5, decoder_1_out6, decoder_1_out7, decoder_1_out8, decoder_1_out9);
  or MEM8 (MEM8_out, decoder_1_out12, decoder_1_out13, decoder_1_out14, decoder_1_out15, decoder_1_out16, decoder_1_out17, decoder_1_out18);
  assign Fetch = FIRST10_out ? in_1 : 1'bz;  // Controlled_Buffer controlled_buffer_1
  assign Decode = decoder_1_out10 ? in_1 : 1'bz;  // Controlled_Buffer controlled_buffer_2
  assign Execute = decoder_1_out11 ? in_1 : 1'bz;  // Controlled_Buffer controlled_buffer_3
  assign Memory = MEM8_out ? in_1 : 1'bz;  // Controlled_Buffer controlled_buffer_4
  assign PC_WB = decoder_1_out21 ? in_1 : 1'bz;  // Controlled_Buffer controlled_buffer_5
  assign PC_update = decoder_1_out0 ? in_1 : 1'bz;  // Controlled_Buffer controlled_buffer_6
  assign mem_read = or_1_out ? in_1 : 1'bz;  // Controlled_Buffer controlled_buffer_7
endmodule

module Inst_and_Need (
  input  in_1,
  input  in_2,
  input  in_3,
  input  in_4,
  output halt,
  output nop,
  output irmovq,
  output needValC,
  output needRegID,
  output push_or_pop,
  output valid_inst
);

  wire decoder_1_out2, decoder_1_out4, decoder_1_out5, decoder_1_out6, decoder_1_out7, decoder_1_out10,
       decoder_1_out11;

  Decoder #(.select(4)) decoder_1 (
    .out0(halt), .out1(nop), .out2(decoder_1_out2), .out3(irmovq), .out4(decoder_1_out4),
    .out5(decoder_1_out5), .out6(decoder_1_out6), .out7(decoder_1_out7), .out10(decoder_1_out10),
    .out11(decoder_1_out11), .sel({in_4, in_3, in_2, in_1}));  // open: out8, out9, out12, out13, out14, out15, en
  or valC (needValC, irmovq, decoder_1_out4, decoder_1_out5, decoder_1_out7);
  or regID (needRegID, decoder_1_out2, irmovq, decoder_1_out4, decoder_1_out5, decoder_1_out6, decoder_1_out10, decoder_1_out11);
  or pushORpop (push_or_pop, decoder_1_out11, decoder_1_out10);
  or inst_valid (valid_inst, halt, nop, decoder_1_out2, irmovq, decoder_1_out4, decoder_1_out5, decoder_1_out6, decoder_1_out10, decoder_1_out11, decoder_1_out7);
endmodule
